// Logisim project Full Adder with D Flip-Flop.circ as structural Verilog: 1 circuit, main circuit main
module main (
  input  x,
  input  y,
  output S
);

  wire and_1_out, and_2_out, c_out, clock_1_out, d_ff_1_q, xor_1_out;

  D_Flip_Flop d_ff_1 (.clk(clock_1_out), .D(c_out), .Q(d_ff_1_q));  // open: Qn, preset, en, reset
  Clock clock_1 (.out(clock_1_out));
  xor xor_1 (xor_1_out, x, y);
  and and_1 (and_1_out, x, y);
  xor xor_2 (S, xor_1_out, d_ff_1_q);
  and and_2 (and_2_out, xor_1_out, d_ff_1_q);
  or c (c_out, and_2_out, and_1_out);
endmodule
